# Fritzing sketch ESP8266ProgrammerBoard (saved by Fritzing 0.9.3b)
breadboards: 1

parts:
  VCC1 = Battery
  Reset_BTN = Pushbutton [package="[THT]"]
  PRGM_BTN = Pushbutton [package="[THT]"]
  10k_Pull-Up = Resistor [tolerance=±5% resistance=10k package=THT]
  10k_Pull-Up_2 = Resistor [tolerance=±5% resistance=10k package=THT]
  ESP8266_Connector = Generic double row female header - 8 pins [form="♀ (female)" package=THT]
  RxTx = female pin header, 2 pins [form="♀ (female)"]
  220Ohm = Resistor [tolerance=±5% resistance=220 package=THT]
  LED1 = LEDs [package=led10mm]

nets:
  GND: VCC1.-, Reset_BTN.Pin_3, Reset_BTN.Pin_4, PRGM_BTN.Pin_3, PRGM_BTN.Pin_4, ESP8266_Connector.GND, 220Ohm.Pin_1
  3.3V: VCC1.+, 10k_Pull-Up.Pin_0, 10k_Pull-Up_2.Pin_0, ESP8266_Connector.Vcc_3.3v
  Reset: Reset_BTN.Pin_1, Reset_BTN.Pin_2, 10k_Pull-Up_2.Pin_1, ESP8266_Connector.Reset
  N1: PRGM_BTN.Pin_1, PRGM_BTN.Pin_2, ESP8266_Connector.GPIO_0
  N2: 10k_Pull-Up.Pin_1, ESP8266_Connector.Ch\PD
  Tx: ESP8266_Connector.Tx, RxTx.pin2
  Rx: ESP8266_Connector.Rx, RxTx.pin1
  GPIO2: ESP8266_Connector.GPIO2, LED1.A
  N3: 220Ohm.Pin_0, LED1.C

custom parts:
  Generic double row female header - 8 pins: Generic double row female header
